# Fritzing sketch TDK_Circuit_diagram (saved by Fritzing 0.9.3b)

parts:
  元件1 = Arduino Mega 2560 (Rev3)
  M1 = DC Motor
  M2 = DC Motor
  S1 = H-Bridge with L298N
  S3 = Round Pushbutton
  U1 = LM2596 step down module
  BAT1 = LIPO-2000mAh [package=lipo-2000]
  BAT2 = LIPO-2000mAh [package=lipo-2000]
  S4 = H-Bridge with L298N
  M4 = DC Motor
  M5 = DC Motor
  元件2 = Voltmeter
  U2 = TRANSCHIPTC5747 [package=camera_sfv24r-2st_2]
  元件3 = Arduino Mega 2560 (Rev3)
  元件4 = Arduino Mega 2560 (Rev3)
  U3 = TRANSCHIPTC5747 [package=camera_sfv24r-2st_2]  # not connected
  J1 = Basic Servo
  J2 = Basic Servo
  J3 = Basic Servo
  J4 = Basic Servo
  J5 = Basic Servo
  S5 = H-Bridge with L298N
  M6 = DC Motor
  M7 = DC Motor
  U8 = HC-SR04 [chip_label=IC package="SIP (Single Inline) [THT]"]
  U9 = HC-SR04 [chip_label=IC package="SIP (Single Inline) [THT]"]
  U10 = HC-SR04 [chip_label=IC package="SIP (Single Inline) [THT]"]
  U11 = HC-SR04 [chip_label=IC package="SIP (Single Inline) [THT]"]

nets:
  VCC: 元件1.5V, U8.Vcc, U9.Vcc, U10.Vcc, U11.Vcc
  GND: 元件1.GND, S1.GND, U1.IN-, U1.OUT-, BAT1.-, BAT2.-, S4.GND, 元件2.GND, 元件3.GND, 元件4.GND, J1.gnd, J2.gnd, J4.gnd, U8.GND, U9.GND, U10.GND, U11.GND
  VIN: 元件1.VIN, S1.5V, U1.OUT+, S4.5V, 元件3.VIN, 元件4.VIN
  N1: 元件1.D2_PWM, S1.ENA
  N2: 元件1.D3_PWM, S1.ENB
  N3: 元件1.D4_PWM, S4.ENA
  N4: 元件1.D5_PWM, S4.ENB
  N5: 元件1.D6_PWM, S5.ENA
  N6: 元件1.D7_PWM, S5.ENB
  N7: 元件1.D30, S5.IN4
  N8: 元件1.D32, S5.IN3
  N9: 元件1.D34, S5.IN2
  N10: 元件1.D36, S5.IN1
  N11: 元件1.D38, S4.IN4
  N12: 元件1.D39, U11.Echo
  N13: 元件1.D40, S4.IN3
  N14: 元件1.D41, U11.Trig
  N15: 元件1.D42, S4.IN2
  N16: 元件1.D43, U10.Echo
  N17: 元件1.D44, S4.IN1
  N18: 元件1.D45, U10.Trig
  N19: 元件1.D46, S1.IN4
  N20: 元件1.D47, U9.Echo
  N21: 元件1.D48, S1.IN3
  N22: 元件1.D49, U9.Trig
  N23: 元件1.D50, S1.IN2
  N24: 元件1.D51, U8.Echo
  N25: 元件1.D52, S1.IN1
  N26: 元件1.D53, U8.Trig
  N27: M1.pin_1, S1.M2-02
  N28: M1.pin_2, S1.M2-01
  N29: M2.pin_1, S4.M2-02
  N30: M2.pin_2, S4.M2-01
  12V: S1.12V, S3.leg1, U1.IN+, S4.12V, 元件2.Vcc
  N31: S1.M1-01, M4.pin_2
  N32: S1.M1-02, M4.pin_1
  N33: S3.leg0, BAT1.+, BAT2.+
  N34: S4.M1-01, M5.pin_2
  N35: S4.M1-02, M5.pin_1
  N36: U2.DOUT_3, U2.DOUT_4
  5V: 元件3.5V, J1.vcc
  N37: 元件3.D2_PWM, J1.pulse
  VCC_2: 元件4.5V, J2.vcc, J3.vcc, J4.vcc, J5.vcc
  N38: 元件4.D2_PWM, J5.pulse
  N39: 元件4.D3_PWM, J4.pulse
  N40: 元件4.D4_PWM, J3.pulse
  N41: 元件4.D5_PWM, J2.pulse
  N42: S5.M1-01, M6.pin_2
  N43: S5.M1-02, M6.pin_1
  N44: S5.M2-01, M7.pin_2
  N45: S5.M2-02, M7.pin_1

notes:
  12000mAh鋰離子電池

custom parts:
  H-Bridge with L298N: h-bridge
  LM2596 step down module: LM2596 DC-DC step down power supply module 3 A.
  HC-SR04: HC-SR04 ultrasound distance sensor
